# Fritzing sketch UCB_usb_power (saved by Fritzing 0.9.6b)

parts:
  Raspberry_Pi_1 = Raspberry Pi 3 [part_number=RPI-3-V1.2]
  U1 = LCD-16X2 [package=lcd-16x2]  # not connected
  S1 = Round Pushbutton
  S2 = Round Pushbutton
  J1 = Piezo Speaker
  LED1 = LED - 3mm [color="Green (570nm)" current=0.030 package="3 mm [THT]"]
  LED2 = LED - 3mm [color="Red (633nm)" current=0.030 package="3 mm [THT]"]
  LED3 = LED - 3mm [color="Orange (620nm)" current=0.030 package="3 mm [THT]"]
  R5 = Resistor [tolerance=±5% power=0.25 resistance=470 package=THT]
  R7 = Resistor [tolerance=±5% power=0.25 resistance=470 package=THT]
  R8 = Resistor [tolerance=±5% power=0.25 resistance=470 package=THT]
  S3 = SPST Switch [package=switch-spst-smd-a]
  X2 = USB Connectors [package=usb-b-pth-vertical]

nets:
  N1: Raspberry_Pi_1.GND, S1.leg0, J1.pin1, LED1.cathode, LED2.cathode, LED3.cathode, S3.P
  N2: Raspberry_Pi_1.GIPO26, J1.pin2
  N3: Raspberry_Pi_1.GIPO21, R8.Pin_1
  N4: Raspberry_Pi_1.GIPO20, R7.Pin_1
  N5: Raspberry_Pi_1.GIPO16, R5.Pin_1
  N6: Raspberry_Pi_1.GIPO24, S2.leg0
  N7: Raspberry_Pi_1.GIPO23, S1.leg1
  N8: Raspberry_Pi_1.5V, X2.VBUS

notes:
  SDA
  SCL
  VCC GND
